# Fritzing sketch Schéma electronique PIC V4 (saved by Fritzing 0.9.5d)
circuit board: 18.6015cm x 12.5524cm
breadboards: 1

parts:
  LCD_16x2_I2C = LCD-16X2 [package=lcd-16x2]
  ARDUINO_UNO = Arduino Leonardo (Rev3b)
  JOYSTICK = Thumb Joystick
  LM393 = GP1A57HR [package=gp1a57hr]
  A4988 = Pololu A4988 [package=SO16]
  NEMA_17 = Stepper Motor - Bipolar
  MG955 = Basic Servo
  Switch = SPST Switch [part_number="Switch End Stop" package=switch-spdt_kit]
  J1 = Power Jack [package=power_jack_smd]
  C1 = Electrolytic Capacitor [capacitance=1000μF package="1010 [SMD, electrolytic]"]
  LM2596 = RioRand LM2596
  C_10nF = Capacitor [package=cap-pth-large]
  NE555 = General purpose bipolar Timer [package=dil-08]

nets:
  N1: LCD_16x2_I2C.DB6, ARDUINO_UNO.A4
  N2: LCD_16x2_I2C.DB7, ARDUINO_UNO.A5
  VCC: LCD_16x2_I2C.A, ARDUINO_UNO.VIN, JOYSTICK.VCC, LM393.2, LM393.4, A4988.MS1, A4988.MS2, A4988.MS3, A4988.VDD, MG955.vcc, LM2596.Pin_3, NE555._RES, NE555.VCC+
  GND: LCD_16x2_I2C.K, ARDUINO_UNO.GND, JOYSTICK.GND, LM393.1, LM393.5, A4988.GND#8, MG955.gnd, Switch.P, LM2596.Pin_4, C_10nF.2, NE555.GND
  N3: ARDUINO_UNO.D2/SDA, ARDUINO_UNO.SDA, NE555.OUT
  N4: ARDUINO_UNO.D3_PWM/SCL, ARDUINO_UNO.SCL, Switch.S
  N5: ARDUINO_UNO.D4/A6, MG955.pulse
  N6: ARDUINO_UNO.D5_PWM, JOYSTICK.SEL
  N7: ARDUINO_UNO.A0, JOYSTICK.HORZ
  N8: ARDUINO_UNO.A1, JOYSTICK.VERT
  N9: ARDUINO_UNO.D8/A8, A4988.DIR
  N10: ARDUINO_UNO.D9_PWM/A9, A4988.STEP
  N11: ARDUINO_UNO.D10_PWM/A10, A4988.ENABLE
  N12: LM393.3, NE555.TRI, NE555.TRE
  N13: A4988.RESET, A4988.SLEEP
  N14: A4988.1B, NEMA_17.D
  N15: A4988.1A, NEMA_17.B
  N16: A4988.2A, NEMA_17.C
  N17: A4988.2B, NEMA_17.A
  N18: A4988.GND#14, J1.GNDBREAK, C1.-, LM2596.Pin_2
  N19: A4988.VMOT, J1.PWR, C1.+, LM2596.Pin_1
  N20: C_10nF.1, NE555.CON
